// Logisim project 20BCE323_20BCE307_20BCE301_RAM.circ as structural Verilog: 1 circuit, main circuit main
module main (
  input  in_1,
  input  in_2,
  input  in_3,
  input  in_4,
  input  in_5,
  input  [1:0] in_6,
  input  Read___Write,
  output out_8,
  output out_9,
  output out_10,
  output out_11
);

  wire and_1_out, and_2_out, and_3_out, and_4_out, and_5_out, and_6_out, and_7_out, and_8_out, and_9_out,
       and_10_out, and_11_out, and_12_out, and_13_out, and_14_out, and_15_out, and_16_out, and_17_out,
       and_18_out, and_19_out, and_20_out, and_21_out, and_22_out, and_23_out, and_24_out, and_25_out,
       and_26_out, and_27_out, and_28_out, and_29_out, and_30_out, and_31_out, and_32_out, and_33_out,
       and_34_out, and_35_out, and_36_out, and_37_out, and_38_out, and_39_out, and_40_out, and_41_out,
       and_42_out, and_43_out, and_44_out, and_45_out, and_46_out, and_47_out, and_48_out, and_49_out,
       and_50_out, and_51_out, clock_1_out, clock_2_out, clock_3_out, clock_4_out, decoder_1_out0,
       decoder_1_out1, decoder_1_out2, decoder_1_out3, not_1_out, not_2_out, not_3_out, not_4_out, not_5_out,
       not_6_out, not_7_out, not_8_out, not_9_out, not_10_out, not_11_out, not_12_out, not_13_out,
       not_14_out, not_15_out, not_16_out, not_17_out, not_18_out, not_19_out, not_20_out, not_21_out,
       not_22_out, not_23_out, not_24_out, not_25_out, not_26_out, not_27_out, not_28_out, not_29_out,
       not_30_out, not_31_out, not_32_out, not_33_out, not_34_out, s_r_ff_1_q, s_r_ff_2_q, s_r_ff_3_q,
       s_r_ff_4_q, s_r_ff_5_q, s_r_ff_6_q, s_r_ff_7_q, s_r_ff_8_q, s_r_ff_9_q, s_r_ff_10_q, s_r_ff_11_q,
       s_r_ff_12_q, s_r_ff_13_q, s_r_ff_14_q, s_r_ff_15_q, s_r_ff_16_q, s_r_ff_17_q, undriven, undriven_2,
       undriven_3;

  Decoder #(.select(2)) decoder_1 (
    .out0(decoder_1_out0), .out1(decoder_1_out1), .out2(decoder_1_out2), .out3(decoder_1_out3), .sel(in_6),
    .en(in_5));
  not not_1 (not_1_out, undriven);
  and and_1 (and_1_out, undriven_3, not_1_out, not_2_out);
  and and_2 (and_2_out, undriven_3, undriven, not_2_out);
  not not_2 (not_2_out, undriven_2);
  S_R_Flip_Flop s_r_ff_1 (.S(and_2_out), .R(and_1_out), .Q(s_r_ff_1_q));  // open: clk, Qn, preset, reset, en
  not not_3 (not_3_out, in_1);
  not not_4 (not_4_out, in_1);
  not not_5 (not_5_out, in_1);
  not not_6 (not_6_out, in_1);
  and and_3 (and_3_out, undriven_3, s_r_ff_1_q, undriven_2);
  Clock clock_1 (.out(clock_1_out));
  and and_4 (and_4_out, decoder_1_out0, not_3_out, not_7_out);
  and and_5 (and_5_out, decoder_1_out0, in_1, not_7_out);
  not not_7 (not_7_out, Read___Write);
  and and_6 (and_6_out, decoder_1_out1, not_4_out, not_8_out);
  and and_7 (and_7_out, decoder_1_out1, in_1, not_8_out);
  not not_8 (not_8_out, Read___Write);
  and and_8 (and_8_out, decoder_1_out2, not_5_out, not_9_out);
  and and_9 (and_9_out, decoder_1_out2, in_1, not_9_out);
  not not_9 (not_9_out, Read___Write);
  and and_10 (and_10_out, decoder_1_out3, not_6_out, not_10_out);
  and and_11 (and_11_out, decoder_1_out3, in_1, not_10_out);
  not not_10 (not_10_out, Read___Write);
  S_R_Flip_Flop s_r_ff_2 (
    .S(and_5_out), .clk(clock_1_out), .R(and_4_out), .Q(s_r_ff_2_q));  // open: Qn, preset, reset, en
  S_R_Flip_Flop s_r_ff_3 (
    .S(and_7_out), .clk(clock_1_out), .R(and_6_out), .Q(s_r_ff_3_q));  // open: Qn, preset, reset, en
  S_R_Flip_Flop s_r_ff_4 (
    .S(and_9_out), .clk(clock_1_out), .R(and_8_out), .Q(s_r_ff_4_q));  // open: Qn, preset, reset, en
  S_R_Flip_Flop s_r_ff_5 (
    .S(and_11_out), .clk(clock_1_out), .R(and_10_out), .Q(s_r_ff_5_q));  // open: Qn, preset, reset, en
  and and_12 (and_12_out, decoder_1_out0, s_r_ff_2_q, Read___Write);
  and and_13 (and_13_out, decoder_1_out1, s_r_ff_3_q, Read___Write);
  and and_14 (and_14_out, decoder_1_out2, s_r_ff_4_q, Read___Write);
  and and_15 (and_15_out, decoder_1_out3, s_r_ff_5_q, Read___Write);
  or or_1 (out_8, and_15_out, and_14_out, and_13_out, and_12_out);
  not not_11 (not_11_out, in_2);
  not not_12 (not_12_out, in_2);
  not not_13 (not_13_out, in_2);
  not not_14 (not_14_out, in_2);
  and and_16 (and_16_out, decoder_1_out0, not_11_out, not_15_out);
  and and_17 (and_17_out, decoder_1_out0, in_2, not_15_out);
  not not_15 (not_15_out, Read___Write);
  and and_18 (and_18_out, decoder_1_out1, not_12_out, not_16_out);
  and and_19 (and_19_out, decoder_1_out1, in_2, not_16_out);
  not not_16 (not_16_out, Read___Write);
  and and_20 (and_20_out, decoder_1_out2, not_13_out, not_17_out);
  and and_21 (and_21_out, decoder_1_out2, in_2, not_17_out);
  not not_17 (not_17_out, Read___Write);
  and and_22 (and_22_out, decoder_1_out3, not_14_out, not_18_out);
  and and_23 (and_23_out, decoder_1_out3, in_2, not_18_out);
  not not_18 (not_18_out, Read___Write);
  Clock clock_2 (.out(clock_2_out));
  S_R_Flip_Flop s_r_ff_6 (
    .S(and_17_out), .clk(clock_2_out), .R(and_16_out), .Q(s_r_ff_6_q));  // open: Qn, preset, reset, en
  S_R_Flip_Flop s_r_ff_7 (
    .S(and_19_out), .clk(clock_2_out), .R(and_18_out), .Q(s_r_ff_7_q));  // open: Qn, preset, reset, en
  S_R_Flip_Flop s_r_ff_8 (
    .S(and_21_out), .clk(clock_2_out), .R(and_20_out), .Q(s_r_ff_8_q));  // open: Qn, preset, reset, en
  S_R_Flip_Flop s_r_ff_9 (
    .S(and_23_out), .clk(clock_2_out), .R(and_22_out), .Q(s_r_ff_9_q));  // open: Qn, preset, reset, en
  and and_24 (and_24_out, decoder_1_out0, s_r_ff_6_q, Read___Write);
  and and_25 (and_25_out, decoder_1_out1, s_r_ff_7_q, Read___Write);
  and and_26 (and_26_out, decoder_1_out2, s_r_ff_8_q, Read___Write);
  and and_27 (and_27_out, decoder_1_out3, s_r_ff_9_q, Read___Write);
  or or_2 (out_9, and_27_out, and_26_out, and_25_out, and_24_out);
  not not_19 (not_19_out, in_3);
  not not_20 (not_20_out, in_3);
  not not_21 (not_21_out, in_3);
  not not_22 (not_22_out, in_3);
  Clock clock_3 (.out(clock_3_out));
  and and_28 (and_28_out, decoder_1_out0, not_19_out, not_23_out);
  and and_29 (and_29_out, decoder_1_out0, in_3, not_23_out);
  not not_23 (not_23_out, Read___Write);
  and and_30 (and_30_out, decoder_1_out1, not_20_out, not_24_out);
  and and_31 (and_31_out, decoder_1_out1, in_3, not_24_out);
  not not_24 (not_24_out, Read___Write);
  and and_32 (and_32_out, decoder_1_out2, not_21_out, not_25_out);
  and and_33 (and_33_out, decoder_1_out2, in_3, not_25_out);
  not not_25 (not_25_out, Read___Write);
  and and_34 (and_34_out, decoder_1_out3, not_22_out, not_26_out);
  and and_35 (and_35_out, decoder_1_out3, in_3, not_26_out);
  not not_26 (not_26_out, Read___Write);
  S_R_Flip_Flop s_r_ff_10 (
    .S(and_29_out), .clk(clock_3_out), .R(and_28_out), .Q(s_r_ff_10_q));  // open: Qn, preset, reset, en
  S_R_Flip_Flop s_r_ff_11 (
    .S(and_31_out), .clk(clock_3_out), .R(and_30_out), .Q(s_r_ff_11_q));  // open: Qn, preset, reset, en
  S_R_Flip_Flop s_r_ff_12 (
    .S(and_33_out), .clk(clock_3_out), .R(and_32_out), .Q(s_r_ff_12_q));  // open: Qn, preset, reset, en
  S_R_Flip_Flop s_r_ff_13 (
    .S(and_35_out), .clk(clock_3_out), .R(and_34_out), .Q(s_r_ff_13_q));  // open: Qn, preset, reset, en
  and and_36 (and_36_out, decoder_1_out0, s_r_ff_10_q, Read___Write);
  and and_37 (and_37_out, decoder_1_out1, s_r_ff_11_q, Read___Write);
  and and_38 (and_38_out, decoder_1_out2, s_r_ff_12_q, Read___Write);
  and and_39 (and_39_out, decoder_1_out3, s_r_ff_13_q, Read___Write);
  or or_3 (out_10, and_39_out, and_38_out, and_37_out, and_36_out);
  not not_27 (not_27_out, in_4);
  not not_28 (not_28_out, in_4);
  not not_29 (not_29_out, in_4);
  not not_30 (not_30_out, in_4);
  Clock clock_4 (.out(clock_4_out));
  and and_40 (and_40_out, decoder_1_out0, not_27_out, not_31_out);
  and and_41 (and_41_out, decoder_1_out0, in_4, not_31_out);
  not not_31 (not_31_out, Read___Write);
  and and_42 (and_42_out, decoder_1_out1, not_28_out, not_32_out);
  and and_43 (and_43_out, decoder_1_out1, in_4, not_32_out);
  not not_32 (not_32_out, Read___Write);
  and and_44 (and_44_out, decoder_1_out2, not_29_out, not_33_out);
  and and_45 (and_45_out, decoder_1_out2, in_4, not_33_out);
  not not_33 (not_33_out, Read___Write);
  and and_46 (and_46_out, decoder_1_out3, not_30_out, not_34_out);
  and and_47 (and_47_out, decoder_1_out3, in_4, not_34_out);
  not not_34 (not_34_out, Read___Write);
  S_R_Flip_Flop s_r_ff_14 (
    .S(and_41_out), .clk(clock_4_out), .R(and_40_out), .Q(s_r_ff_14_q));  // open: Qn, preset, reset, en
  S_R_Flip_Flop s_r_ff_15 (
    .S(and_43_out), .clk(clock_4_out), .R(and_42_out), .Q(s_r_ff_15_q));  // open: Qn, preset, reset, en
  S_R_Flip_Flop s_r_ff_16 (
    .S(and_45_out), .clk(clock_4_out), .R(and_44_out), .Q(s_r_ff_16_q));  // open: Qn, preset, reset, en
  S_R_Flip_Flop s_r_ff_17 (
    .S(and_47_out), .clk(clock_4_out), .R(and_46_out), .Q(s_r_ff_17_q));  // open: Qn, preset, reset, en
  and and_48 (and_48_out, decoder_1_out0, s_r_ff_14_q, Read___Write);
  and and_49 (and_49_out, decoder_1_out1, s_r_ff_15_q, Read___Write);
  and and_50 (and_50_out, decoder_1_out2, s_r_ff_16_q, Read___Write);
  and and_51 (and_51_out, decoder_1_out3, s_r_ff_17_q, Read___Write);
  or or_4 (out_11, and_51_out, and_50_out, and_49_out, and_48_out);

  // Notes on the sheet:
  //   Memory Enable
  //   Address Input
  //   Input
  //   2 x 4 decoder
  //   Read - 1
  //   Write - 0
  //   Binary Storage Cell Logic Diagram
  //   Select
  //   Read / Write
  //   4 x 4bit RAM logic circuit
  //   Output
  //   Implementation Of Storage Device (RAM) Using Logisim
  //   Input Data
  //   Output Data
  //   Submitted By :-
  //          20BCE307 - Mufid Vohra
  //   20BCE323 - Yati Tank
  //   20BCE301 - Unnat Shah
endmodule
